// Logisim project exe4.circ as structural Verilog: 1 circuit, main circuit main
module main (
  input  in_1
);

  wire clock_1_out, d_ff_1_q, d_ff_1_qn, d_ff_2_q, d_ff_2_qn, d_ff_3_q;

  Clock clock_1 (.out(clock_1_out));
  D_Flip_Flop d_ff_1 (.clk(clock_1_out), .D(in_1), .Q(d_ff_1_q), .Qn(d_ff_1_qn));  // open: preset, reset
  LED led_1 (.in(d_ff_1_qn));
  LED led_2 (.in(d_ff_2_q));
  D_Flip_Flop d_ff_2 (.clk(clock_1_out), .D(d_ff_1_q), .Q(d_ff_2_q), .Qn(d_ff_2_qn));  // open: preset, reset
  D_Flip_Flop d_ff_3 (.clk(clock_1_out), .D(d_ff_2_qn), .Q(d_ff_3_q));  // open: Qn, preset, reset
  LED led_3 (.in(d_ff_3_q));
endmodule
