// Logisim project ex3.circ as structural Verilog: 2 circuits, main circuit main
module main (
  input  in_1,
  input  EQ,
  input  in_3
);

  wire undriven;

  BitEquality bitequality_1 (.a(in_1), .in_2(undriven), .b(in_3));
  BitEquality bitequality_2 (.in_2(undriven));  // open: a, b
  BitEquality bitequality_3 ();  // open: a, in_2, b
  BitEquality bitequality_4 ();  // open: a, in_2, b
  BitEquality bitequality_5 ();  // open: a, in_2, b
endmodule

module BitEquality (
  input  a,
  input  in_2,
  input  b
);

  xnor xnor_1 (in_2, a, b);
endmodule
