// Logisim project ex3.circ as structural Verilog: 1 circuit, main circuit main
module main (
  input  in_1,
  input  in_2
);

  wire clock_1_out, j_k_ff_1_qn, j_k_ff_2_qn;

  Clock clock_1 (.out(clock_1_out));
  J_K_Flip_Flop j_k_ff_1 (.J(in_1), .clk(clock_1_out), .K(in_2), .Qn(j_k_ff_1_qn));  // open: Q, preset, reset
  J_K_Flip_Flop j_k_ff_2 (
    .J(j_k_ff_1_qn), .clk(clock_1_out), .K(j_k_ff_1_qn), .Qn(j_k_ff_2_qn));  // open: Q, preset, reset
  J_K_Flip_Flop j_k_ff_3 (.J(j_k_ff_2_qn), .clk(clock_1_out), .K(j_k_ff_2_qn));  // open: Q, Qn, preset, reset
endmodule
