// Logisim project exe5.circ as structural Verilog: 1 circuit, main circuit main
module main (
  input  in_1
);

  wire clock_1_out, t_ff_1_q, t_ff_2_q, t_ff_3_q;

  Clock clock_1 (.out(clock_1_out));
  T_Flip_Flop t_ff_1 (.clk(clock_1_out), .T(in_1), .Q(t_ff_1_q));  // open: Qn, preset, reset
  T_Flip_Flop t_ff_2 (.clk(t_ff_1_q), .T(in_1), .Q(t_ff_2_q));  // open: Qn, preset, reset
  T_Flip_Flop t_ff_3 (.clk(t_ff_2_q), .T(in_1), .Q(t_ff_3_q));  // open: Qn, preset, reset
  T_Flip_Flop t_ff_4 (.clk(t_ff_3_q), .T(in_1));  // open: Q, Qn, preset, reset
endmodule
