// Logisim project atividadepratica01.circ as structural Verilog: 5 circuits, main circuit main
module main (
  input  A1,
  input  in_2,
  input  A2,
  input  A3,
  input  A4,
  input  B1,
  input  B2,
  input  B3,
  input  B4,
  output out_10,
  output out_11,
  output out_12,
  output out_13,
  output out_14,
  output out_15
);

  wire decodificador_1_l0, decodificador_1_l1, decodificador_1_l2, decodificador_1_l3, decodificador_1_l4,
       decodificador_1_l5, decodificador_1_l6, decodificador_2_l0, decodificador_2_l1, decodificador_2_l2,
       decodificador_2_l3, decodificador_2_l4, decodificador_2_l5, decodificador_2_l6, decodificador_3_l0,
       decodificador_3_l1, decodificador_3_l2, decodificador_3_l3, decodificador_3_l4, decodificador_3_l5,
       decodificador_3_l6;

  decodificador decodificador_1 (
    .A0(A4), .A1(A3), .A2(A2), .A3(A1), .L0(decodificador_1_l0), .L1(decodificador_1_l1),
    .L2(decodificador_1_l2), .L3(decodificador_1_l3), .L4(decodificador_1_l4), .L5(decodificador_1_l5),
    .L6(decodificador_1_l6));
  decodificador decodificador_2 (
    .A0(B4), .A1(B3), .A2(B2), .A3(B1), .L0(decodificador_2_l0), .L1(decodificador_2_l1),
    .L2(decodificador_2_l2), .L3(decodificador_2_l3), .L4(decodificador_2_l4), .L5(decodificador_2_l5),
    .L6(decodificador_2_l6));
  _7_Segment_Display u_7_segment_display_1 (
    .g(decodificador_1_l3), .f(decodificador_1_l2), .a(decodificador_1_l1), .b(decodificador_1_l0),
    .e(decodificador_1_l4), .d(decodificador_1_l5), .c(decodificador_1_l6));  // open: dp
  somador4Bits somador4bits_1 (
    .a1(A1), .b1(B1), .a2(A2), .b2(B2), .a3(A3), .b3(B3), .a4(A4), .b4(B4), .s1(out_13), .s2(out_12),
    .s3(out_11), .s4(out_10), .Overflow(out_14), .Co1(out_15), .Ci1(in_2));
  _7_Segment_Display u_7_segment_display_2 (
    .g(decodificador_2_l3), .f(decodificador_2_l2), .a(decodificador_2_l1), .b(decodificador_2_l0),
    .e(decodificador_2_l4), .d(decodificador_2_l5), .c(decodificador_2_l6));  // open: dp
  decodificador decodificador_3 (
    .A0(out_10), .A1(out_11), .A2(out_12), .A3(out_13), .L0(decodificador_3_l0), .L1(decodificador_3_l1),
    .L2(decodificador_3_l2), .L3(decodificador_3_l3), .L4(decodificador_3_l4), .L5(decodificador_3_l5),
    .L6(decodificador_3_l6));
  _7_Segment_Display u_7_segment_display_3 (
    .g(decodificador_3_l3), .f(decodificador_3_l2), .a(decodificador_3_l1), .b(decodificador_3_l0),
    .e(decodificador_3_l4), .d(decodificador_3_l5), .c(decodificador_3_l6));  // open: dp
endmodule

module meiaSoma (
  input  x1,
  input  x2,
  output S1,
  output Co1
);

  xor xor_1 (S1, x1, x2);
  and and_1 (Co1, x1, x2);
endmodule

module somaCompleta (
  input  X1,
  input  X2,
  input  Ci1,
  output S1,
  output Co1
);

  wire meiasoma_1_co1, meiasoma_1_s1, meiasoma_2_co1;

  meiaSoma meiasoma_1 (.x1(X1), .x2(X2), .S1(meiasoma_1_s1), .Co1(meiasoma_1_co1));
  or or_1 (Co1, meiasoma_1_co1, meiasoma_2_co1);
  meiaSoma meiasoma_2 (.x1(meiasoma_1_s1), .x2(Ci1), .S1(S1), .Co1(meiasoma_2_co1));
endmodule

module somador4Bits (
  input  Ci1,
  input  a1,
  input  b1,
  input  a2,
  input  b2,
  input  a3,
  input  b3,
  input  a4,
  input  b4,
  output s1,
  output s2,
  output s3,
  output s4,
  output Co1,
  output Overflow
);

  wire somacompleta_1_co1, somacompleta_2_co1, somacompleta_3_co1;

  somaCompleta somacompleta_1 (.X1(a1), .X2(b1), .Ci1(Ci1), .S1(s1), .Co1(somacompleta_1_co1));
  somaCompleta somacompleta_2 (.X1(a2), .X2(b2), .Ci1(somacompleta_1_co1), .S1(s2), .Co1(somacompleta_2_co1));
  somaCompleta somacompleta_3 (.X1(a3), .X2(b3), .Ci1(somacompleta_2_co1), .S1(s3), .Co1(somacompleta_3_co1));
  somaCompleta somacompleta_4 (.X1(a4), .X2(b4), .Ci1(somacompleta_3_co1), .S1(s4), .Co1(Co1));
  xor xor_1 (Overflow, Co1, somacompleta_3_co1);
endmodule

module decodificador (
  input  A0,
  input  A1,
  input  A2,
  input  A3,
  output L0,
  output L1,
  output L2,
  output L3,
  output L4,
  output L5,
  output L6
);

  wire and_1_out, and_2_out, and_3_out, and_4_out, and_5_out, and_6_out, and_7_out, and_8_out, and_9_out,
       and_10_out, and_11_out, and_12_out, and_13_out, and_14_out, and_15_out, and_16_out, and_17_out,
       and_18_out, and_19_out, and_20_out, and_21_out, and_22_out, and_23_out, and_24_out, and_25_out,
       and_26_out, and_27_out, and_28_out, and_29_out, and_30_out, and_31_out, and_32_out, and_33_out,
       and_34_out, and_35_out, and_36_out, and_37_out, and_38_out, and_39_out, and_40_out, and_41_out,
       and_42_out, and_43_out, and_44_out, and_45_out, not_1_out, not_2_out, not_3_out, not_4_out, not_5_out,
       not_6_out, not_7_out, not_8_out, not_9_out, not_10_out, not_11_out, not_12_out, not_13_out,
       not_14_out, not_15_out, not_16_out, not_17_out, not_18_out, not_19_out, not_20_out, not_21_out,
       not_22_out, not_23_out, not_24_out, not_25_out, not_26_out, not_27_out, not_28_out, not_29_out,
       not_30_out, not_31_out, not_32_out, not_33_out, not_34_out, not_35_out, not_36_out, not_37_out,
       not_38_out, not_39_out, not_40_out, not_41_out, not_42_out, or_1_out, or_2_out, or_3_out, or_4_out,
       or_5_out, or_6_out, or_7_out, or_8_out, or_9_out, or_11_out, or_12_out, or_14_out, or_15_out,
       or_16_out, or_17_out, or_18_out, or_19_out, or_20_out, or_22_out, or_23_out;

  not not_1 (not_1_out, A0);
  not not_2 (not_2_out, A1);
  not not_3 (not_3_out, A0);
  and and_1 (and_1_out, not_3_out, not_4_out);
  not not_4 (not_4_out, A2);
  not not_5 (not_5_out, A3);
  not not_6 (not_6_out, A0);
  not not_7 (not_7_out, A2);
  not not_8 (not_8_out, A1);
  not not_9 (not_9_out, A3);
  not not_10 (not_10_out, A0);
  not not_11 (not_11_out, A0);
  and and_2 (and_2_out, A0, not_12_out);
  not not_12 (not_12_out, A1);
  not not_13 (not_13_out, A2);
  not not_14 (not_14_out, A2);
  and and_3 (and_3_out, not_14_out, not_15_out);
  not not_15 (not_15_out, A3);
  not not_16 (not_16_out, A0);
  and and_4 (and_4_out, not_16_out, A1);
  and and_5 (and_5_out, A0, not_17_out);
  not not_17 (not_17_out, A1);
  and and_6 (and_6_out, A0, A2);
  not not_18 (not_18_out, A1);
  and and_7 (and_7_out, not_18_out, A2);
  and and_8 (and_8_out, A2, not_19_out);
  not not_19 (not_19_out, A3);
  not not_20 (not_20_out, A0);
  and and_9 (and_9_out, not_20_out, A1);
  not not_21 (not_21_out, A2);
  not not_22 (not_22_out, A1);
  not not_23 (not_23_out, A1);
  and and_10 (and_10_out, not_23_out, not_24_out);
  not not_24 (not_24_out, A3);
  and and_11 (and_11_out, A2, not_25_out);
  not not_25 (not_25_out, A3);
  and and_12 (and_12_out, A0, A2);
  and and_13 (and_13_out, A0, A1);
  not not_26 (not_26_out, A0);
  and and_14 (and_14_out, not_26_out, not_27_out);
  not not_27 (not_27_out, A1);
  not not_28 (not_28_out, A3);
  not not_29 (not_29_out, A1);
  and and_15 (and_15_out, not_29_out, A2);
  not not_30 (not_30_out, A2);
  not not_31 (not_31_out, A2);
  not not_32 (not_32_out, A0);
  and and_16 (and_16_out, not_32_out, not_33_out);
  not not_33 (not_33_out, A2);
  not not_34 (not_34_out, A0);
  and and_17 (and_17_out, not_34_out, A3);
  not not_35 (not_35_out, A2);
  not not_36 (not_36_out, A0);
  not not_37 (not_37_out, A1);
  and and_18 (and_18_out, not_1_out, not_2_out);
  and and_19 (and_19_out, and_1_out, not_5_out);
  not not_38 (not_38_out, A1);
  not not_39 (not_39_out, A3);
  and and_20 (and_20_out, not_6_out, A2);
  and and_21 (and_21_out, A0, not_7_out);
  and and_22 (and_22_out, not_8_out, not_9_out);
  and and_23 (and_23_out, not_10_out, A2);
  and and_24 (and_24_out, not_11_out, A1);
  and and_25 (and_25_out, A1, A2);
  and and_26 (and_26_out, and_2_out, not_13_out);
  not not_40 (not_40_out, A3);
  or or_1 (or_1_out, and_3_out, and_4_out);
  or or_2 (or_2_out, and_5_out, and_6_out);
  or or_3 (or_3_out, and_7_out, and_8_out);
  and and_27 (and_27_out, and_9_out, not_21_out);
  and and_28 (and_28_out, A0, not_22_out);
  and and_29 (and_29_out, A0, A3);
  or or_4 (or_4_out, and_10_out, and_11_out);
  or or_5 (or_5_out, and_12_out, and_13_out);
  and and_30 (and_30_out, and_14_out, not_28_out);
  and and_31 (and_31_out, and_15_out, A3);
  and and_32 (and_32_out, A1, not_30_out);
  and and_33 (and_33_out, A1, A2);
  not not_41 (not_41_out, A3);
  and and_34 (and_34_out, A0, not_31_out);
  not not_42 (not_42_out, A3);
  or or_6 (or_6_out, and_16_out, and_17_out);
  and and_35 (and_35_out, not_35_out, A3);
  and and_36 (and_36_out, not_36_out, A1);
  and and_37 (and_37_out, A0, not_37_out);
  or or_7 (or_7_out, and_18_out, and_19_out);
  and and_38 (and_38_out, not_38_out, not_39_out);
  and and_39 (and_39_out, and_20_out, A3);
  and and_40 (and_40_out, and_21_out, A3);
  or or_8 (or_8_out, and_22_out, and_23_out);
  and and_41 (and_41_out, and_24_out, A3);
  or or_9 (or_9_out, and_25_out, and_26_out);
  and and_42 (and_42_out, A0, not_40_out);
  or or_10 (L2, or_1_out, or_2_out);
  or or_11 (or_11_out, or_3_out, and_27_out);
  or or_12 (or_12_out, and_28_out, and_29_out);
  or or_13 (L4, or_4_out, or_5_out);
  or or_14 (or_14_out, and_30_out, and_31_out);
  and and_43 (and_43_out, and_32_out, A3);
  and and_44 (and_44_out, and_33_out, not_41_out);
  and and_45 (and_45_out, and_34_out, not_42_out);
  or or_15 (or_15_out, or_6_out, and_35_out);
  or or_16 (or_16_out, and_36_out, and_37_out);
  or or_17 (or_17_out, or_7_out, and_38_out);
  or or_18 (or_18_out, and_39_out, and_40_out);
  or or_19 (or_19_out, or_8_out, and_41_out);
  or or_20 (or_20_out, or_9_out, and_42_out);
  or or_21 (L3, or_11_out, or_12_out);
  or or_22 (or_22_out, or_14_out, and_43_out);
  or or_23 (or_23_out, and_44_out, and_45_out);
  or or_24 (L6, or_15_out, or_16_out);
  or or_25 (L0, or_17_out, or_18_out);
  or or_26 (L1, or_19_out, or_20_out);
  or or_27 (L5, or_22_out, or_23_out);
endmodule
