// Logisim project ep02.circ as structural Verilog
module ULA1bit (
  input  [1:0] Select,
  input  Binvert,
  input  Carry_in,
  input  a,
  input  b,
  output Resultado,
  output Carry_out
);

  wire adder_1_out, and_1_out, multiplexer_1_out, not_1_out, not_2_out, or_1_out;

  Multiplexer #(.enable("false")) multiplexer_1 (.in0(b), .in1(not_1_out), .out(multiplexer_1_out), .sel(Binvert));
  not not_1 (not_1_out, b);
  and and_1 (and_1_out, a, multiplexer_1_out);
  or or_1 (or_1_out, a, multiplexer_1_out);
  not not_2 (not_2_out, a);
  Adder #(.width(1)) adder_1 (.a(a), .b(multiplexer_1_out), .out(adder_1_out), .cin(Carry_in), .cout(Carry_out));
  Multiplexer #(.select(2), .enable("false")) multiplexer_2 (
    .in0(and_1_out), .in1(or_1_out), .in2(not_2_out), .in3(adder_1_out), .out(Resultado), .sel(Select));
endmodule

module ULA4bits (
  input  [1:0] Select,
  input  B3,
  input  B2,
  input  B1,
  input  B0,
  input  A3,
  input  A2,
  input  A1,
  input  A0,
  input  Binvert,
  output S0,
  output S1,
  output S2,
  output S3,
  output Cout
);

  wire ula1bit_1_carry_out, ula1bit_2_carry_out, ula1bit_3_carry_out;

  ULA1bit ula1bit_1 (
    .a(A0), .b(B0), .Binvert(Binvert), .Carry_in(Binvert), .Select(Select), .Carry_out(ula1bit_1_carry_out),
    .Resultado(S0));
  ULA1bit ula1bit_2 (
    .a(A1), .b(B1), .Binvert(Binvert), .Carry_in(ula1bit_1_carry_out), .Select(Select),
    .Carry_out(ula1bit_2_carry_out), .Resultado(S1));
  ULA1bit ula1bit_3 (
    .a(A2), .b(B2), .Binvert(Binvert), .Carry_in(ula1bit_2_carry_out), .Select(Select),
    .Carry_out(ula1bit_3_carry_out), .Resultado(S2));
  ULA1bit ula1bit_4 (
    .a(A3), .b(B3), .Binvert(Binvert), .Carry_in(ula1bit_3_carry_out), .Select(Select), .Carry_out(Cout),
    .Resultado(S3));
endmodule

module ULA74LS181 (
  input  [3:0] in_1,
  input  [3:0] A,
  input  [3:0] B,
  output [3:0] out_4
);

  wire [3:0] and_1_out, and_2_out, and_3_out, nand_1_out, nor_1_out, not_1_out, not_2_out, not_3_out,
       not_4_out, not_5_out, not_6_out, or_1_out, or_2_out, or_3_out, xor_1_out, xor_2_out;

  assign not_1_out = ~B;  // NOT_Gate not_1, 4 bits wide
  assign not_2_out = ~A;  // NOT_Gate not_2, 4 bits wide
  assign not_3_out = ~B;  // NOT_Gate not_3, 4 bits wide
  assign not_4_out = ~A;  // NOT_Gate not_4, 4 bits wide
  assign not_5_out = ~A;  // NOT_Gate not_5, 4 bits wide
  assign and_1_out = A & not_1_out;  // AND_Gate and_1, 4 bits wide
  assign or_1_out = not_2_out | B;  // OR_Gate or_1, 4 bits wide
  assign xor_1_out = A ^ B;  // XOR_Gate xor_1, 4 bits wide
  assign and_2_out = A & B;  // AND_Gate and_2, 4 bits wide
  assign or_2_out = A | not_3_out;  // OR_Gate or_2, 4 bits wide
  assign or_3_out = A | B;  // OR_Gate or_3, 4 bits wide
  assign nor_1_out = ~(A | A);  // NOR_Gate nor_1, 4 bits wide
  assign and_3_out = not_5_out & B;  // AND_Gate and_3, 4 bits wide
  assign nand_1_out = ~(A & B);  // NAND_Gate nand_1, 4 bits wide
  assign not_6_out = ~B;  // NOT_Gate not_6, 4 bits wide
  assign xor_2_out = A ^ B;  // XOR_Gate xor_2, 4 bits wide
  Multiplexer #(.select(4), .width(4), .enable("false")) multiplexer_1 (
    .in0(not_4_out), .in1(nor_1_out), .in2(and_3_out), .in3(4'b0000), .in4(nand_1_out), .in5(not_6_out),
    .in6(xor_2_out), .in7(and_1_out), .in8(or_1_out), .in9(xor_1_out), .in10(B), .in11(and_2_out),
    .in12(4'b0001), .in13(or_2_out), .in14(or_3_out), .in15(A), .out(out_4), .sel(in_1));
endmodule
